# Fritzing sketch MAIN (saved by Fritzing 1.0.5)

parts:
  esp1 = ESP32 DevKitc V4
  DC_Mot_Enc1 = DC Motor with two-phase hall-encoder [part_number=VT-E-G25A-06-177E]
  DC_Mot_Enc2 = DC Motor with two-phase hall-encoder [part_number=VT-E-G25A-06-177E]
  A1 = motor driver ZK-5AD
  U1 = LM2596 step down module
  VCC1 = Battery
  SPKR1 = Loudspeaker
  M1 = RPlidar A1M8 [package=THT]
  Part1 = Adafruit MAX98357A I2S 3W Class D Amplifier [part_number="Adafruit #3006"]
  LCD1 = TFT 1.8 inch 160x128 w SD
  LCD2 = TFT 1.8 inch 160x128 w SD
  S1 = Toggle Switch [package=THT]

nets:
  N1: esp1.IO15, DC_Mot_Enc1.pin4
  N2: esp1.IO2, DC_Mot_Enc1.pin3
  N3: esp1.IO4, LCD1.pin_5
  N4: esp1.IO17, M1.pin2
  N5: esp1.IO5, LCD1.pin3
  N6: esp1.IO18, LCD1.pin_7, LCD2.pin_7
  N7: esp1.IO21, Part1.LRCLK
  N8: esp1.IO22, Part1.DIN
  N9: esp1.IO23, LCD1.pin_6, LCD2.pin_6
  GND: esp1.GND, DC_Mot_Enc1.pin5, DC_Mot_Enc2.pin5, A1.Pin_12, U1.IN-, U1.OUT-, VCC1.-, M1.pin4, Part1.GND, LCD1.pin2, LCD2.pin2
  N10: esp1.3V3, LCD1.pin_1, LCD2.pin_1
  N11: esp1.IO34, DC_Mot_Enc2.pin3
  N12: esp1.IO35, DC_Mot_Enc2.pin4
  N13: esp1.IO32, A1.Pin_6
  N14: esp1.IO33, A1.Pin_5
  N15: esp1.IO25, A1.Pin_3
  N16: esp1.IO26, A1.Pin_4
  N17: esp1.IO27, LCD1.pin4
  N18: esp1.IO14, LCD2.pin4
  N19: esp1.IO12, LCD2.pin_5
  N20: esp1.IO13, LCD2.pin3
  5V: esp1.5V, DC_Mot_Enc1.pin2, DC_Mot_Enc2.pin2, U1.OUT+, M1.pin3, Part1.VIN, LCD1.pin_8, LCD2.pin_8
  N21: esp1.D1, Part1.BCLK
  N22: DC_Mot_Enc1.pin1, A1.Pin_11
  N23: DC_Mot_Enc1.pin6, A1.Pin_10
  N24: DC_Mot_Enc2.pin1, A1.Pin_9
  N25: DC_Mot_Enc2.pin6, A1.Pin_8
  N26: A1.Pin_13, U1.IN+, S1.L2
  N27: VCC1.+, S1.COM
  N28: SPKR1.pin1, Part1.VO-
  N29: SPKR1.pin2, Part1.VO+

notes:
  R
  L

custom parts:
  ESP32 DevKitc V4: ESP32-DevKitC board with ESP32-WROOM-32 module. ESP32-DevKitC V4 is a small-sized ESP32-based development board produced by Espressif. Most of the pins on the ESP module are broken out to the pin headers on the board. The pins D0, D1, D2, D3, CMD and CLK are used internally for communication between ESP32 and SPI flash memory. They are grouped on both sides near the USB connector. Avoid using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
  motor driver ZK-5AD: 5A Dual Motor Drive Module Reverse PWM Speed Regulation Double H Bridge L298N Module DC 3.0V-14V.
  LM2596 step down module: LM2596 DC-DC step down power supply module 3 A.
  Battery: Your standard 2x 18650 battery pack (7.4 Volts)
  RPlidar A1M8: .The RPLIDAR A1 is the next generation low cost 360 degree 2D laser scanner (LIDAR) solution developed by SLAMTEC. It can take up to 4000 samples of laser ranging per second with high rotation speed. And equipped with SLAMTEC patented OPTMAG technology, it breakouts the life limitation of traditional LIDAR system so as to work stably for a long time.
  Adafruit MAX98357A I2S 3W Class D Amplifier: Listen to this good news - we now have an all in one digital audio amp breakout board that works incredibly well with the Raspberry Pi! If you're looking for an easy and low cost way to get you digital sound files bumpin' then the MAX08357 I2S Amp Breakout is for you. It takes standard I2S digital audio input and, not only decodes it into analog, but also amplifies it directly into a speaker.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
  TFT 1.8 inch 160x128 w SD: This is a generic 1.8 tft spi lcd display available on ebay and others. The 1.8" display has 128x160 color pixels.
